# Fritzing sketch connection (saved by Fritzing 1.0.5)
breadboards: 1

parts:
  Yumo-enc1 = YumoE6B2
  R1 = Resistor [tolerance=±5% resistance=4.7k package="0402 [SMD]"]
  R2 = Resistor [tolerance=±5% resistance=4.7k package="0402 [SMD]"]
  Part1 = Arduino Mega 2560 (Rev3)
  U1 = SWITCH_SPDT [package=kps-1290]
  R3 = Resistor [tolerance=±5% resistance=4.7k package="0402 [SMD]"]
  Pololu_A1 = Pololu A4988 [package=SO16]
  C1 = Electrolytic Capacitor [capacitance=100μF voltage=35V package="0807 [SMD, electrolytic]"]
  M1 = Stepper Motor - Bipolar
  VCC1 = 4 x AAA Battery Mount [internal_resistance=0.1Ω]
  VCC2 = Battery block 9V [internal_resistance=0.1Ω]
  VCC3 = Battery [internal_resistance=0.1Ω]

nets:
  N1: Yumo-enc1.V, R1.Pin_1, R2.Pin_1, U1.O, R3.Pin_1, Pololu_A1.VDD, VCC1.+
  N2: Yumo-enc1.A, R1.Pin_0, Part1.D2_PWM
  N3: Yumo-enc1.B, R2.Pin_0, Part1.D3_PWM
  GND: Yumo-enc1.GND, Part1.GND, U1.S, Pololu_A1.GND, C1.-, VCC1.-, VCC2.-, VCC3.-
  N4: Part1.D4_PWM, Pololu_A1.STEP
  N5: Part1.D5_PWM, Pololu_A1.DIR
  N6: Part1.D6_PWM, U1.P, R3.Pin_0
  N7: Pololu_A1.RESET, Pololu_A1.SLEEP
  N8: Pololu_A1.1B, M1.D
  N9: Pololu_A1.1A, M1.B
  N10: Pololu_A1.2A, M1.C
  N11: Pololu_A1.2B, M1.A
  N12: Pololu_A1.VMOT, C1.+, VCC2.+, VCC3.+
